# Fritzing sketch GY-NEO6MV2 (saved by Fritzing 0.9.3b)
circuit board: 8.46667cm x 5.64444cm

parts:
  GY-NEO6MV2 = SUP500F [package=sup500f]
  Raspberry_Pi_3B+ = Raspberry Pi 3 [part_number=RPI-3-V1.2]

nets:
  N1: GY-NEO6MV2.RX-I, Raspberry_Pi_3B+.GPIO14
  N2: GY-NEO6MV2.TX-O, Raspberry_Pi_3B+.GPIO15
  GND: GY-NEO6MV2.GND, Raspberry_Pi_3B+.GND
  3V3: GY-NEO6MV2.VCC, Raspberry_Pi_3B+.3v3, Raspberry_Pi_3B+.3V3

notes:
  RX
  TX
  GND
  VCC
